# Fritzing sketch CompleteToyWiring (saved by Fritzing 0.9.3b)
breadboards: 1

parts:
  Part1 = HC-SR501 Body Sensor Module
  J1 = Basic Servo
  Raspberry_Pi_1 = Raspberry Pi 3 [part_number=RPI-3-V1.2]
  Power_plug1 = Power plug
  U1 = TCM8240MD [package=tcm8240md]  # not connected

nets:
  VCC: Part1.VCC, Raspberry_Pi_1.5V
  N1: Part1.OUT, Raspberry_Pi_1.GPIO17
  GND: Part1.GND, J1.gnd, Raspberry_Pi_1.GND, Power_plug1.GND
  VCC_2: J1.vcc, Power_plug1.VCC
  N2: J1.pulse, Raspberry_Pi_1.GPIO18

custom parts:
  HC-SR501 Body Sensor Module: Pyroelectric Infrared PIR Motion Sensor Detector Module
